# Fritzing sketch prototype (saved by Fritzing 0.9.2b)

parts:
  Part1 = Arduino Uno (Rev3)
  Part2 = Bluetooth HM-10
  Part4 = Arduino Nano (Rev3.0)
  Part5 = Bluetooth HM-10

nets:
  N1: Part1.D10_PWM/SS, Part2.TXD
  N2: Part1.D11_PWM/MOSI, Part2.RXD
  3V3: Part1.3V3, Part2.VCC, Part2.STATE
  GND: Part1.GND, Part2.GND
  N3: Part4.D10, Part5.TXD
  N4: Part4.D11/MOSI, Part5.RXD
  GND_2: Part4.GND, Part5.GND
  3V3_2: Part4.3V3, Part5.VCC, Part5.STATE
